// Logisim project micro.circ as structural Verilog: 1 circuit, main circuit EV20_Superescalar
module EV20_Superescalar (
);

  wire bloque1_1_preload, button_1_out, CLK, CLK2, CLK3, CLK4, dipswitch_1_sw1, not_1_out, not_2_out,
       not_3_out, pipeline_register_2_p11, pipeline_register_2_p12, selector_a_1_p2, UC1_ALU_EN, UC1_LS_EN,
       undriven, undriven_2;
  wire [3:0] pipeline_register_1_p5;
  wire [5:0] selector_c_1_busc_selector;
  wire [9:0] UC1_ALU_DADRES, UC1_LS_DADRES;
  wire [10:0] ProgramCounterReg_ia0ia10;
  wire [14:0] MicroInstructionROM_microinstruction;
  wire [15:0] BusA_ALU_q, BusB_ALU_q;
  wire [23:0] BBUS, ProgramMemory_data;
  wire [30:0] UC1_ALU_SD, UC1_LS_SD;

  ROM #(.addrWidth(11), .dataWidth(24)) ProgramMemory (.addr(ProgramCounterReg_ia0ia10), .data(ProgramMemory_data));
  Bloque1 bloque1_1 (.B12B11(BBUS[12:11]), .Preload(bloque1_1_preload));  // open: WRegister, CY
  PCreg ProgramCounterReg (
    .Preload(bloque1_1_preload), .HOLD(undriven), .B0B10(BBUS[10:0]), .IA0IA10(ProgramCounterReg_ia0ia10));  // open: CLK1
  Register #(.width(24)) InstructionRegister (.D(ProgramMemory_data), .en(undriven), .Q(BBUS));  // open: clk, clr
  not not_1 (not_1_out, UC1_ALU_EN);
  // Selector_A selector_a_1: pin names not known; wires that end beside it: BBUS, selector_a_1_p2
  // Pipeline_register pipeline_register_1: pin names not known; wires that end beside it: 1'b0, UC1_ALU_SD, UC1_ALU_DADRES, not_1_out, pipeline_register_1_p5
  Selector_C selector_c_1 (.BusB(BBUS), .BusC_Selector(selector_c_1_busc_selector));
  Micro_Instruction_ROM MicroInstructionROM (
    .Instruction(BBUS), .MicroInstruction(MicroInstructionROM_microinstruction));
  Register #(.width(16)) BusA_ALU (.D(16'hbbbb), .en(UC1_ALU_EN), .Q(BusA_ALU_q));  // open: clk, clr
  Register #(.width(16)) BusB_ALU (.D(16'hcccc), .en(UC1_ALU_EN), .Q(BusB_ALU_q));  // open: clk, clr
  // Pipeline_register pipeline_register_2: pin names not known; wires that end beside it: MicroInstructionROM_microinstruction[14:11], MicroInstructionROM_microinstruction[10:9], MicroInstructionROM_microinstruction[8], 1'b1, MicroInstructionROM_microinstruction[7:6], BBUS[14:10], MicroInstructionROM_microinstruction[5:0], selector_c_1_busc_selector, selector_a_1_p2, BBUS[14:5], pipeline_register_2_p11, pipeline_register_2_p12
  not not_2 (not_2_out, undriven_2);
  ALU ALUALULAU (.ALUC(pipeline_register_1_p5), .A(BusA_ALU_q), .B(BusB_ALU_q));  // open: CYin, Z, CYout
  Pipeline_register pipeline_register_3 (
    .S_low_P_high(1'b0), .Hold(not_2_out));  // open: ALUC_IN, SH_IN, Kmx_IN, CLK, MRyMB_IN, B_bus_IN, T_bus_IN, C_bus_IN, Serial_IN, A_bus_IN, D_Address_IN, ALUC_OUT, SH_OUT, Kmx_OUT, MRyMB_OUT, B_bus_OUT, T_bus_OUT, C_bus_OUT, Serial_OUT, A_bus_OUT, D_Address_OUT
  // UC1 uc1_1: pin names not known; wires that end beside it: pipeline_register_2_p11, pipeline_register_2_p12, UC1_ALU_EN, UC1_LS_EN, UC1_ALU_SD, UC1_LS_SD, UC1_ALU_DADRES
  not not_3 (not_3_out, UC1_LS_EN);
  DipSwitch #(.number(2)) dipswitch_1 (.sw1(dipswitch_1_sw1));  // open: sw2
  Button button_1 (.out(button_1_out));
  Register #(.width(16)) BusA_LS (.D(16'haaaa));  // open: en, clk, Q, clr
  ClockGenerator clocks (
    .Auto(dipswitch_1_sw1), .ManualCLK(button_1_out), .CLK(CLK), .CLK2(CLK2), .CLK3(CLK3), .CLK4(CLK4));
  // Pipeline_register LoadStore: pin names not known; wires that end beside it: 1'b0, UC1_LS_SD, UC1_LS_DADRES, not_3_out

  // Notes on the sheet:
  //   BUS B
endmodule
